// Logisim project TallerLogica-Combinatorios-individual.circ as structural Verilog: 11 circuits, main circuit verificador
module sumador_simple (
  input  A,
  input  B,
  output S,
  output Cout
);

  xor xor_1 (S, A, B);
  and and_1 (Cout, A, B);
endmodule

module sumador_completo (
  input  Cin,
  input  A,
  input  B,
  output S,
  output Cout
);

  wire sumador_simple_1_cout, sumador_simple_1_s, sumador_simple_2_cout;

  sumador_simple sumador_simple_1 (.A(A), .B(B), .S(sumador_simple_1_s), .Cout(sumador_simple_1_cout));
  sumador_simple sumador_simple_2 (.A(Cin), .B(sumador_simple_1_s), .S(S), .Cout(sumador_simple_2_cout));
  or or_1 (Cout, sumador_simple_2_cout, sumador_simple_1_cout);
endmodule

module sumador_4 (
  input  Cin,
  input  [3:0] A,
  input  [3:0] B,
  output [3:0] S,
  output Cout
);

  wire sumador_completo_1_cout, sumador_completo_2_cout, sumador_completo_3_cout;

  sumador_completo sumador_completo_1 (.Cin(Cin), .A(A[0]), .B(B[0]), .S(S[0]), .Cout(sumador_completo_1_cout));
  sumador_completo sumador_completo_2 (
    .Cin(sumador_completo_1_cout), .A(A[1]), .B(B[1]), .S(S[1]), .Cout(sumador_completo_2_cout));
  sumador_completo sumador_completo_3 (
    .Cin(sumador_completo_2_cout), .A(A[2]), .B(B[2]), .S(S[2]), .Cout(sumador_completo_3_cout));
  sumador_completo sumador_completo_4 (.Cin(sumador_completo_3_cout), .A(A[3]), .B(B[3]), .S(S[3]), .Cout(Cout));
  Hex_Digit_Display hex_digit_display_1 (.value(S));  // open: dp
endmodule

module comparador_cero (
  input  [3:0] A,
  output Z
);

  wire not_1_out, not_2_out, or_1_out, or_2_out;

  or or_1 (or_1_out, A[0], A[1]);
  not not_1 (not_1_out, or_1_out);
  or or_2 (or_2_out, A[2], A[3]);
  not not_2 (not_2_out, or_2_out);
  and and_1 (Z, not_1_out, not_2_out);
endmodule

module sumador_flags (
  input  Cin,
  input  [3:0] A,
  input  [3:0] B,
  output Z,
  output [3:0] S,
  output C,
  output N,
  output V
);

  sumador_4 sumador_4_1 (.Cin(Cin), .A(A), .B(B), .S({N, S[2:0]}), .Cout(C));
  comp_overflow comp_overflow_1 (.c3(N), .a3(A[3]), .b3(B[3]), .O(V));
  Hex_Digit_Display hex_digit_display_1 (.value({N, S[2:0]}));  // open: dp
  comparador_cero comparador_cero_1 (.A({N, S[2:0]}), .Z(Z));

  assign S[3] = N;
endmodule

module incrementador_4 (
  input  [3:0] A,
  output [3:0] S
);

  sumador_4 sumador_4_1 (.A(A), .B(4'b0001), .S(S));  // open: Cin, Cout
  Hex_Digit_Display hex_digit_display_1 (.value(S));  // open: dp
endmodule

module inversor_4 (
  input  [3:0] A,
  input  INV,
  output [3:0] S
);

  wire [3:0] incrementador_4_1_s, not_1_out;

  not not_1 (not_1_out[0], A[0]);
  not not_2 (not_1_out[1], A[1]);
  not not_3 (not_1_out[2], A[2]);
  not not_4 (not_1_out[3], A[3]);
  Multiplexer #(.width(4)) multiplexer_1 (.in0(A), .in1(incrementador_4_1_s), .out(S), .sel(INV));
  incrementador_4 incrementador_4_1 (.A(not_1_out), .S(incrementador_4_1_s));
  Hex_Digit_Display hex_digit_display_1 (.value(S));  // open: dp
endmodule

module ALU (
  input  [3:0] A,
  input  [3:0] B,
  input  [1:0] OP,
  output N,
  output Z,
  output V,
  output C,
  output [3:0] S
);

  wire and_o_or, multiplexer_3_out, multiplexer_5_out, not_1_out, not_3_out, not_4_out, op3, or_1_out,
       or_2_out, overflow_resta_1_v_out, resta, suma, sumador_flags_1_c, sumador_flags_1_v;
  wire [0:0] comparador_cero_1_z;
  wire [3:0] and_3_out, inversor_4_1_s, or_4_out, s1, s2;

  not not_1 (not_1_out, OP[1]);
  or or_1 (or_1_out, OP[0], OP[1]);
  and and_1 (resta, OP[0], not_1_out);
  and and_2 (and_o_or, OP[0], OP[1]);
  or or_2 (or_2_out, or_1_out, resta);
  not not_2 (suma, or_1_out);
  not not_3 (not_3_out, 1'b1);
  inversor_4 inversor_4_1 (.A(B), .INV(or_2_out), .S(inversor_4_1_s));
  Multiplexer #(.width(4)) multiplexer_1 (.in0(s2), .in1(s1), .out({N, S[2:0]}), .sel(op3));
  or or_3 (op3, suma, resta);
  Hex_Digit_Display hex_digit_display_1 (.value({N, S[2:0]}));  // open: dp
  sumador_flags sumador_flags_1 (
    .Cin(not_3_out), .A(A), .B(inversor_4_1_s), .S(s1), .C(sumador_flags_1_c), .V(sumador_flags_1_v));  // open: Z, N
  assign and_3_out = A & B;  // AND_Gate and_3, 4 bits wide
  assign or_4_out = A | B;  // OR_Gate or_4, 4 bits wide
  Multiplexer #(.width(4)) multiplexer_2 (.in0(and_3_out), .in1(or_4_out), .out(s2), .sel(and_o_or));
  not not_4 (not_4_out, sumador_flags_1_c);
  comparador_cero comparador_cero_1 (.A(B), .Z(comparador_cero_1_z[0]));
  comparador_cero comparador_cero_2 (.A({N, S[2:0]}), .Z(Z));
  Multiplexer #(.select(2)) multiplexer_3 (
    .in0(sumador_flags_1_c), .in1(sumador_flags_1_c), .in2(not_4_out), .in3(1'b0), .out(multiplexer_3_out),
    .sel({resta, comparador_cero_1_z[0]}));
  overflow_resta overflow_resta_1 (.V_in(sumador_flags_1_v), .B(B), .V_out(overflow_resta_1_v_out));
  Multiplexer multiplexer_4 (.in0(1'b0), .in1(multiplexer_3_out), .out(C), .sel(op3));
  Multiplexer multiplexer_5 (
    .in0(sumador_flags_1_v), .in1(overflow_resta_1_v_out), .out(multiplexer_5_out), .sel(resta));
  Multiplexer multiplexer_6 (.in0(1'b0), .in1(multiplexer_5_out), .out(V), .sel(op3));

  assign S[3] = N;

  // Other names for the same wires on the sheet: r_final[3:0] = {N, S[2:0]}
endmodule

module verificador (
  output [3:0] out_1,
  output [3:0] out_2,
  output [1:0] out_3,
  output halt,
  output N,
  output Z,
  output V,
  output C,
  output [3:0] res
);

  wire clock_1_out;

  Clock clock_1 (.out(clock_1_out));
  Counter #(.max('h3ff), .width(10)) counter_1 (
    .clk(clock_1_out), .carry(halt), .Q({out_3, out_2, out_1}));  // open: clr, load, up, count, D
  ALU alu_1 (.A(out_1), .B(out_2), .OP(out_3), .N(N), .Z(Z), .V(V), .C(C), .S(res));
endmodule

module overflow_resta (
  input  V_in,
  input  [3:0] B,
  output V_out
);

  wire comparador_cero_1_z, not_2_out;
  wire [3:3] not_1_out;

  not not_1 (not_1_out[3], B[3]);
  not not_2 (not_2_out, V_in);
  comparador_cero comparador_cero_1 (.A({not_1_out[3], B[2:0]}), .Z(comparador_cero_1_z));
  Multiplexer multiplexer_1 (.in0(V_in), .in1(not_2_out), .out(V_out), .sel(comparador_cero_1_z));
endmodule

module comp_overflow (
  input  c3,
  input  a3,
  input  b3,
  output O
);

  wire not_1_out, xor_1_out, xor_2_out;

  xor xor_1 (xor_1_out, c3, a3);
  not not_1 (not_1_out, xor_2_out);
  xor xor_2 (xor_2_out, a3, b3);
  and and_1 (O, xor_1_out, not_1_out);
endmodule
